// Logisim project FinalCircuit.circ as structural Verilog: 1 circuit, main circuit main
module main (
  input  W,
  input  X,
  input  Y,
  input  Z,
  input  W_2,
  input  X_2,
  input  Y_2,
  input  Z_2,
  input  W_3,
  input  X_3,
  input  Y_3,
  input  Z_3,
  input  W_4,
  input  X_4,
  input  Y_4,
  input  Z_4,
  input  W_5,
  input  X_5,
  input  Y_5,
  input  Z_5,
  input  W_6,
  input  X_6,
  input  Y_6,
  input  Z_6,
  input  W_7,
  input  X_7,
  input  Y_7,
  input  Z_7
);

  wire A_out, and_1_out, and_2_out, and_3_out, and_4_out, and_5_out, and_6_out, and_7_out, and_8_out,
       and_9_out, and_10_out, and_11_out, and_12_out, and_13_out, and_14_out, and_15_out, and_16_out,
       and_17_out, and_18_out, and_19_out, and_20_out, and_21_out, and_22_out, and_23_out, and_24_out,
       and_25_out, and_26_out, and_27_out, and_28_out, and_29_out, and_30_out, B_out, C_out, D_out, E_out,
       F_out, G_out, or_1_out, or_2_out, or_3_out, or_4_out, or_5_out, or_6_out, or_7_out, or_8_out,
       or_9_out, or_10_out, or_11_out, or_12_out, or_13_out, or_14_out, or_15_out, or_16_out, or_17_out,
       or_18_out;

  not not_1 (Z, Z);
  not not_2 (Z_2, Z_2);
  not not_3 (Z_3, Z_3);
  not not_4 (Z_4, Z_4);
  not not_5 (Z_5, Z_5);
  not not_6 (Z_6, Z_6);
  not not_7 (Z_7, Z_7);
  not not_8 (X, X);
  not not_9 (Y, Y);
  not not_10 (X_2, X_2);
  not not_11 (Y_2, Y_2);
  not not_12 (X_3, X_3);
  not not_13 (Y_3, Y_3);
  not not_14 (X_4, X_4);
  not not_15 (Y_4, Y_4);
  not not_16 (X_5, X_5);
  not not_17 (Y_5, Y_5);
  not not_18 (X_6, X_6);
  not not_19 (Y_6, Y_6);
  not not_20 (X_7, X_7);
  not not_21 (Y_7, Y_7);
  not not_22 (W, W);
  not not_23 (W_2, W_2);
  not not_24 (W_3, W_3);
  not not_25 (W_4, W_4);
  not not_26 (W_5, W_5);
  not not_27 (W_6, W_6);
  not not_28 (W_7, W_7);
  and and_1 (and_1_out, W_2, Y_2, Z_2);
  and and_2 (and_2_out, W_3, X_3);
  and and_3 (and_3_out, W_3, Y_3);
  and and_4 (and_4_out, W_3, Z_3);
  and and_5 (and_5_out, W_4, Y_4, Z_4);
  and and_6 (and_6_out, X_5, Y_5, Z_5);
  and and_7 (and_7_out, X_5, Y_5, Z_5);
  and and_8 (and_8_out, W_5, Y_5, Z_5);
  and and_9 (and_9_out, W_2, Y_2, Z_2);
  or or_1 (or_1_out, and_2_out, and_3_out);
  and and_10 (and_10_out, W_4, X_4, Z_4);
  and and_11 (and_11_out, X_4, Y_4, Z_4);
  or or_2 (or_2_out, and_9_out, and_1_out);
  or or_3 (or_3_out, and_10_out, and_11_out);
  or or_4 (or_4_out, and_7_out, and_8_out);
  and and_12 (and_12_out, W_2, Y_2, Z_2);
  and and_13 (and_13_out, Y_6, Z_6);
  and and_14 (and_14_out, X_6, Y_6, Z_6);
  and and_15 (and_15_out, W_6, X_6);
  and and_16 (and_16_out, W_6, Z_6);
  and and_17 (and_17_out, X_6, Y_6);
  and and_18 (and_18_out, W_3, X_3);
  and and_19 (and_19_out, Y_3, Z_3);
  and and_20 (and_20_out, X_4, Y_4, Z_4);
  and and_21 (and_21_out, X_4, Y_4, Z_4);
  or or_5 (or_5_out, and_13_out, and_14_out);
  or or_6 (or_6_out, and_15_out, and_16_out);
  and and_22 (and_22_out, W_7, X_7);
  and and_23 (and_23_out, W_7, X_7, Y_7);
  and and_24 (and_24_out, X_7, Y_7, Z_7);
  and and_25 (and_25_out, W_7, Y_7);
  and and_26 (and_26_out, X_7, Y_7);
  and and_27 (and_27_out, X, Z);
  and and_28 (and_28_out, X, Y);
  or or_7 (or_7_out, and_20_out, and_21_out);
  and and_29 (and_29_out, W_5, X_5);
  or or_8 (or_8_out, and_22_out, and_23_out);
  or or_9 (or_9_out, and_24_out, and_25_out);
  and and_30 (and_30_out, X, Z);
  or or_10 (or_10_out, X_2, and_12_out);
  or or_11 (or_11_out, and_18_out, and_19_out);
  or or_12 (or_12_out, and_29_out, and_6_out);
  or or_13 (or_13_out, or_5_out, or_6_out);
  or or_14 (or_14_out, W, and_30_out);
  or or_15 (or_15_out, and_27_out, and_28_out);
  or or_16 (or_16_out, or_11_out, or_1_out);
  or or_17 (or_17_out, or_7_out, or_3_out);
  or or_18 (or_18_out, or_8_out, or_9_out);
  or D (D_out, or_17_out, and_5_out);
  or E (E_out, or_12_out, or_4_out);
  or F (F_out, or_13_out, and_17_out);
  or A (A_out, or_14_out, or_15_out);
  or B (B_out, or_10_out, or_2_out);
  or C (C_out, or_16_out, and_4_out);
  or G (G_out, or_18_out, and_26_out);
endmodule
